# Fritzing sketch IOT (saved by Fritzing 0.9.2b)
breadboards: 1

parts:
  Part1 = Arduino Nano (Rev3.0) (ICSP)
  Part2 = SRF05 Ultrasonic Rangefinder
  Part3 = SRF05 Ultrasonic Rangefinder
  U1 = NodeMCU V3.0

nets:
  N1: Part1.D1/TX, U1.RX
  GND: Part1.GND, Part2.GND, Part3.GND
  N2: Part1.D6, Part3.Echo
  N3: Part1.D9, Part3.Trig
  N4: Part1.D10, Part2.Echo
  N5: Part1.D11/MOSI, Part2.Trig
  VCC: Part1.VIN, Part2.VCC, Part3.VCC
  N6: U1.GND#6, U1.GND#13, U1.GND#16, U1.GND#33

custom parts:
  NodeMCU V3.0: ESP8266 based NodeMCU
